# Fritzing sketch robot (saved by Fritzing 1.0.7)

parts:
  Mod1 = Raspberry Pi Pico W
  Mod2 = L298N DC motor driver
  M1 = DC Motor [voltage_(max)=6V voltage_(min)=3V]
  VCC1 = Battery [internal_resistance=0.1Ω]
  M2 = DC Motor [voltage_(max)=6V voltage_(min)=3V]
  Mod3 = L298N DC motor driver
  M3 = DC Motor [voltage_(max)=6V voltage_(min)=3V]
  M4 = DC Motor [voltage_(max)=6V voltage_(min)=3V]
  VCC2 = Battery [internal_resistance=0.1Ω]

nets:
  N1: Mod1.pin_4, Mod2.ENB
  N2: Mod1.pin_5, Mod2.IN4
  N3: Mod1.pin_6, Mod2.IN3
  N4: Mod1.pin_7, Mod2.IN2
  N5: Mod1.pin_9, Mod2.IN1
  N6: Mod1.pin_10, Mod2.ENA
  N7: Mod1.pin_24, Mod3.ENB
  N8: Mod1.pin_25, Mod3.IN4
  N9: Mod1.pin_26, Mod3.IN3
  N10: Mod1.pin_27, Mod3.IN2
  N11: Mod1.pin_29, Mod3.IN1
  N12: Mod1.pin_30, Mod3.ENA
  N13: Mod2.OUT1, M1.pin_2
  N14: Mod2.OUT2, M1.pin_1
  N15: Mod2.12V, Mod2.5V-ENA-JMP-O, VCC1.+
  N16: Mod2.GND, VCC1.-
  N17: Mod2.OUT3, M2.pin_2
  N18: Mod2.OUT4, M2.pin_1
  N19: Mod3.OUT1, M3.pin_2
  N20: Mod3.OUT2, M3.pin_1
  N21: Mod3.12V, Mod3.5V-ENA-JMP-O, VCC2.+
  N22: Mod3.GND, VCC2.-
  N23: Mod3.OUT3, M4.pin_2
  N24: Mod3.OUT4, M4.pin_1

custom parts:
  Raspberry Pi Pico W: Raspberry Pi Pico W. Based around the RP2040 microcontroller the Pico W is a low cost microcontroller device bringing Raspberry Pi quality, cost, and easy of use to the microcontroller space. The areas marked KEEPOUT in pcb silkscreen should not have traces running through them to avoid shorts on a soldered in module!
  L298N DC motor driver: 2x DC motor driver with 78M05 positive voltage regulator (7..35 V) L298N: max 46 V, 2 A Set 5 V Enable jumper to enable 5 V regultor (needed for the L298N) and +5 V output at screw terminal or supply external +5 V at screw terminal Set ENA and/or ENB to +5 V to enable motor permanently or supply ENA and/or ENB with PWM signal IN1 and IN2 set rotation directory for motor A (OUT1/OUT2) IN2 and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
